# Fritzing sketch FritzingSketch (saved by Fritzing 0.9.3b)
breadboards: 1

parts:
  U1 = NodeMCU V3.0
  J1 = Power Jack [package=power_jack_pth_lock]
  M1 = RioRand LM2596
  Q1 = MOSFET-NCHANNEL [part_number=IRF530N package=to220v]
  R1 = Photocell (LDR) [package=THT]
  S1 = Reed switch [package=THT]
  R1_2 = Resistor [tolerance=±5% resistance=10k package=THT]
  PIR1 = PIR sensor
  Part1 = DHT22 module
  SPKR1 = Loudspeaker

nets:
  N1: U1.D0, Q1.G
  N2: U1.D1, S1.pin_1
  3V3: U1.3V3, PIR1.VDD, Part1.VCC
  GND: U1.GND#6, U1.GND#13, U1.GND#16, U1.GND#33, M1.Pin_4, S1.pin_2, R1_2.Pin_1, PIR1.GND, Part1.GND
  N3: U1.D5, PIR1.SIG
  N4: U1.D6, Part1.DATA
  N5: U1.Vin, M1.Pin_3, R1.pin_0
  N6: U1.A0, R1.pin_1, R1_2.Pin_0
  N7: J1.GND, M1.Pin_2, Q1.S
  N8: J1.PWR, M1.Pin_1, SPKR1.pin2
  N9: Q1.D, SPKR1.pin1

notes:
  12v DC

custom parts:
  NodeMCU V3.0: ESP8266 based NodeMCU
